# Fritzing sketch luz_escalera_infrarrojos_uno (saved by Fritzing 0.7.7b)

parts:
  Arduino1 = Arduino
  R2 = Resistor [tolerance=±5% resistance=1k package=THT]
  Q2 = NPN-Transistor [package="TO92 [THT]"]
  LED2 = LED - 5mm [color="Red (633nm)" package="5 mm [THT]"]
  R3 = Resistor [tolerance=±5% resistance=1k package=THT]
  Q3 = NPN-Transistor [package="TO92 [THT]"]
  LED3 = LED - 5mm [color="Red (633nm)" package="5 mm [THT]"]
  R4 = Resistor [tolerance=±5% resistance=1k package=THT]
  Q4 = NPN-Transistor [package="TO92 [THT]"]
  LED4 = LED - 5mm [color="Red (633nm)" package="5 mm [THT]"]
  R5 = Resistor [tolerance=±5% resistance=1k package=THT]
  Q5 = NPN-Transistor [package="TO92 [THT]"]
  LED5 = LED - 5mm [color="Red (633nm)" package="5 mm [THT]"]
  R6 = Resistor [tolerance=±5% resistance=1k package=THT]
  Q6 = NPN-Transistor [package="TO92 [THT]"]
  LED6 = LED - 5mm [color="Red (633nm)" package="5 mm [THT]"]
  R7 = Resistor [tolerance=±5% resistance=1k package=THT]
  Q7 = NPN-Transistor [package="TO92 [THT]"]
  LED7 = LED - 5mm [color="Red (633nm)" package="5 mm [THT]"]
  R8 = Resistor [tolerance=±5% resistance=1k package=THT]
  Q8 = NPN-Transistor [package="TO92 [THT]"]
  LED8 = LED - 5mm [color="Red (633nm)" package="5 mm [THT]"]
  R9 = Resistor [tolerance=±5% resistance=1k package=THT]
  Q9 = NPN-Transistor [package="TO92 [THT]"]
  LED9 = LED - 5mm [color="Red (633nm)" package="5 mm [THT]"]
  R10 = Resistor [tolerance=±5% resistance=1k package=THT]
  Q10 = NPN-Transistor [package="TO92 [THT]"]
  LED10 = LED - 5mm [color="Red (633nm)" package="5 mm [THT]"]
  R11 = Trimmer Potentiometer [maximum_resistance=10kΩ package=THT]
  R12 = Trimmer Potentiometer [maximum_resistance=10kΩ package=THT]
  R13 = Trimmer Potentiometer [maximum_resistance=10kΩ package=THT]
  U3 = mystery part, 3 pins [chip_label=?]
  U4 = Voltage Regulator - 5V [package="TO220 [THT]"]
  Power_plug1 = Power plug
  J1 = Infrared Proximity Sensor
  J2 = Infrared Proximity Sensor
  S1 = Pushbutton [package="[THT]"]
  S2 = Pushbutton [package="[THT]"]
  R14 = Resistor [tolerance=±5% resistance=10k package=THT]
  R15 = Resistor [tolerance=±5% resistance=10k package=THT]

nets:
  GND: Arduino1.GND, U4.GND, Power_plug1.GND, J1.GND, J2.GND
  N1: Arduino1.D12, R10.Pin_0
  N2: Arduino1.D11, R9.Pin_0
  N3: Arduino1.D10, R8.Pin_0
  N4: Arduino1.D9, R7.Pin_0
  N5: Arduino1.D8, R6.Pin_0
  N6: Arduino1.D7, R5.Pin_0
  N7: Arduino1.D6, R4.Pin_0
  N8: Arduino1.D5, R3.Pin_0
  N9: Arduino1.D4, R2.Pin_0
  N10: Arduino1.D3, S2.Pin_3, S2.Pin_4, R15.Pin_0
  N11: Arduino1.D2, S1.Pin_3, S1.Pin_4, R14.Pin_0
  VCC: Arduino1.VIN, U4.output_voltage, J1.Vcc, J2.Vcc, R14.Pin_1, R15.Pin_1
  N12: Arduino1.A0, J2.Vout
  N13: Arduino1.A1, J1.Vout
  N14: Arduino1.A2, U3.pin2
  N15: Arduino1.A3, R11.wiper
  N16: Arduino1.A4, R12.wiper
  N17: Arduino1.A5, R13.wiper
  N18: R2.Pin_1, Q2.E
  N19: Q2.B, LED2.cathode
  N20: Q2.C, Q3.C, Q4.C, Q5.C, Q6.C, Q7.C, Q8.C, Q9.C, Q10.C, R11.leg1, R12.leg1, R13.leg1, U3.pin1, S1.Pin_2, S2.Pin_1, S2.Pin_2
  N21: LED2.anode, LED3.anode, LED4.anode, LED5.anode, LED6.anode, LED7.anode, LED8.anode, LED9.anode, LED10.anode
  N22: R3.Pin_1, Q3.E
  N23: Q3.B, LED3.cathode
  N24: R4.Pin_1, Q4.E
  N25: Q4.B, LED4.cathode
  N26: R5.Pin_1, Q5.E
  N27: Q5.B, LED5.cathode
  N28: R6.Pin_1, Q6.E
  N29: Q6.B, LED6.cathode
  N30: R7.Pin_1, Q7.E
  N31: Q7.B, LED7.cathode
  N32: R8.Pin_1, Q8.E
  N33: Q8.B, LED8.cathode
  N34: R9.Pin_1, Q9.E
  N35: Q9.B, LED9.cathode
  N36: R10.Pin_1, Q10.E
  N37: Q10.B, LED10.cathode
  N38: R11.leg2, R12.leg2, R13.leg2, U3.pin3

notes:
  TIRA DE LED PELDAÑO 1
  TIRA DE LED PELDAÑO 2
  TIRA DE LED PELDAÑO 3
  TIRA DE LED PELDAÑO 4
  TIRA DE LED PELDAÑO 5
  TIRA DE LED PELDAÑO 6
  TIRA DE LED PELDAÑO 7
  TIRA DE LED PELDAÑO 8
  TIRA DE LED PELDAÑO 9
  7805
  12V
  Sensor
  Luz
  LDR
  Ajuste
  Sensor
  Subida
  10k
  Ajuste
  Sensor
  Bajada
  10k
  Ajuste
  Nivel
  de luz
  10k
  B C E
  BD137
  1K
  Sensor Bajar
  Sensor Subir
  Subir
  Tiempo
  Bajar
  Tiempo
