# Fritzing sketch luz_escalera_ultrasonidos_mega (saved by Fritzing 0.7.7b)

parts:
  U1 = Arduino Mega
  R1 = Resistor [tolerance=±5% resistance=1k package=THT]
  Q1 = NPN-Transistor [package="TO92 [THT]"]
  LED1 = LED - 5mm [color="Red (633nm)" package="5 mm [THT]"]
  R2 = Resistor [tolerance=±5% resistance=1k package=THT]
  Q2 = NPN-Transistor [package="TO92 [THT]"]
  LED2 = LED - 5mm [color="Red (633nm)" package="5 mm [THT]"]
  R3 = Resistor [tolerance=±5% resistance=1k package=THT]
  Q3 = NPN-Transistor [package="TO92 [THT]"]
  LED3 = LED - 5mm [color="Red (633nm)" package="5 mm [THT]"]
  R4 = Resistor [tolerance=±5% resistance=1k package=THT]
  Q4 = NPN-Transistor [package="TO92 [THT]"]
  LED4 = LED - 5mm [color="Red (633nm)" package="5 mm [THT]"]
  R5 = Resistor [tolerance=±5% resistance=1k package=THT]
  Q5 = NPN-Transistor [package="TO92 [THT]"]
  LED5 = LED - 5mm [color="Red (633nm)" package="5 mm [THT]"]
  R6 = Resistor [tolerance=±5% resistance=1k package=THT]
  Q6 = NPN-Transistor [package="TO92 [THT]"]
  LED6 = LED - 5mm [color="Red (633nm)" package="5 mm [THT]"]
  R7 = Resistor [tolerance=±5% resistance=1k package=THT]
  Q7 = NPN-Transistor [package="TO92 [THT]"]
  LED7 = LED - 5mm [color="Red (633nm)" package="5 mm [THT]"]
  R8 = Resistor [tolerance=±5% resistance=1k package=THT]
  Q8 = NPN-Transistor [package="TO92 [THT]"]
  LED8 = LED - 5mm [color="Red (633nm)" package="5 mm [THT]"]
  R9 = Resistor [tolerance=±5% resistance=1k package=THT]
  Q9 = NPN-Transistor [package="TO92 [THT]"]
  LED9 = LED - 5mm [color="Red (633nm)" package="5 mm [THT]"]
  R10 = Resistor [tolerance=±5% resistance=1k package=THT]
  Q10 = NPN-Transistor [package="TO92 [THT]"]
  LED10 = LED - 5mm [color="Red (633nm)" package="5 mm [THT]"]
  R11 = Resistor [tolerance=±5% resistance=1k package=THT]
  Q11 = NPN-Transistor [package="TO92 [THT]"]
  LED11 = LED - 5mm [color="Red (633nm)" package="5 mm [THT]"]
  R12 = Resistor [tolerance=±5% resistance=1k package=THT]
  Q12 = NPN-Transistor [package="TO92 [THT]"]
  LED12 = LED - 5mm [color="Red (633nm)" package="5 mm [THT]"]
  R13 = Resistor [tolerance=±5% resistance=1k package=THT]
  Q13 = NPN-Transistor [package="TO92 [THT]"]
  LED13 = LED - 5mm [color="Red (633nm)" package="5 mm [THT]"]
  R14 = Resistor [tolerance=±5% resistance=1k package=THT]
  Q14 = NPN-Transistor [package="TO92 [THT]"]
  LED14 = LED - 5mm [color="Red (633nm)" package="5 mm [THT]"]
  R15 = Resistor [tolerance=±5% resistance=1k package=THT]
  Q15 = NPN-Transistor [package="TO92 [THT]"]
  LED15 = LED - 5mm [color="Red (633nm)" package="5 mm [THT]"]
  R16 = Resistor [tolerance=±5% resistance=1k package=THT]
  Q16 = NPN-Transistor [package="TO92 [THT]"]
  LED16 = LED - 5mm [color="Red (633nm)" package="5 mm [THT]"]
  R17 = Resistor [tolerance=±5% resistance=1k package=THT]
  LED17 = LED - 5mm [color="Red (633nm)" package="5 mm [THT]"]
  Q17 = NPN-Transistor [package="TO92 [THT]"]
  U2 = mystery part, 4 pins [chip_label=?]
  U3 = mystery part, 4 pins [chip_label=?]
  R18 = Trimmer Potentiometer [maximum_resistance=10kΩ package=THT]
  R19 = Trimmer Potentiometer [maximum_resistance=10kΩ package=THT]
  R20 = Trimmer Potentiometer [maximum_resistance=10kΩ package=THT]
  U4 = mystery part, 3 pins [chip_label=?]
  R21 = Resistor [tolerance=±5% resistance=10k package=THT]
  U5 = mystery part, 2 pins [chip_label=?]
  U6 = Voltage Regulator - 5V [package="TO220 [THT]"]
  Power_plug1 = Power plug

nets:
  N1: U1.D13, U3.pin3
  N2: U1.D12, U3.pin2
  N3: U1.D11, U2.pin3
  N4: U1.D10, U2.pin2
  N5: U1.D8, R21.Pin_0, U5.pin2
  GND: U1.GND, U2.pin1, U3.pin1, R18.leg2, R19.leg2, R20.leg2, U4.pin3, R21.Pin_1, U6.GND, Power_plug1.GND
  N6: U1.VIN, U2.pin4, U3.pin4, R18.leg1, R19.leg1, R20.leg1, U4.pin2, U5.pin1, U6.output_voltage
  N7: U1.A0, U4.pin1
  N8: U1.A1, R18.wiper
  N9: U1.A2, R19.wiper
  N10: U1.A3, R20.wiper
  N11: U1.D22, R1.Pin_0
  N12: U1.D23, R17.Pin_0
  N13: U1.D24, R2.Pin_0
  N14: U1.D26, R3.Pin_0
  N15: U1.D28, R4.Pin_0
  N16: U1.D30, R5.Pin_0
  N17: U1.D32, R6.Pin_0
  N18: U1.D34, R7.Pin_0
  N19: U1.D36, R8.Pin_0
  N20: U1.D38, R9.Pin_0
  N21: U1.D40, R10.Pin_0
  N22: U1.D42, R11.Pin_0
  N23: U1.D44, R12.Pin_0
  N24: U1.D46, R13.Pin_0
  N25: U1.D48, R14.Pin_0
  N26: U1.D50, R15.Pin_0
  N27: U1.D52, R16.Pin_0
  N28: R1.Pin_1, Q1.E
  N29: Q1.B, LED1.cathode
  N30: Q1.C, Q2.C, Q3.C, Q4.C, Q5.C, Q6.C, Q7.C, Q8.C, Q9.C, Q10.C, Q11.C, Q12.C, Q13.C, Q14.C, Q15.C, Q16.C
  N31: LED1.anode, U6.input_voltage, Power_plug1.VCC
  N32: R2.Pin_1, Q2.E
  N33: Q2.B, LED2.cathode
  N34: R3.Pin_1, Q3.E
  N35: Q3.B, LED3.cathode
  N36: LED3.anode, LED4.anode, LED5.anode, LED6.anode, LED7.anode
  N37: R4.Pin_1, Q4.E
  N38: Q4.B, LED4.cathode
  N39: R5.Pin_1, Q5.E
  N40: Q5.B, LED5.cathode
  N41: R6.Pin_1, Q6.E
  N42: Q6.B, LED6.cathode
  N43: R7.Pin_1, Q7.E
  N44: Q7.B, LED7.cathode
  N45: R8.Pin_1, Q8.E
  N46: Q8.B, LED8.cathode
  N47: R9.Pin_1, Q9.E
  N48: Q9.B, LED9.cathode
  N49: R10.Pin_1, Q10.E
  N50: Q10.B, LED10.cathode
  N51: R11.Pin_1, Q11.E
  N52: Q11.B, LED11.cathode
  N53: LED11.anode, LED12.anode, LED13.anode, LED14.anode, LED15.anode
  N54: R12.Pin_1, Q12.E
  N55: Q12.B, LED12.cathode
  N56: R13.Pin_1, Q13.E
  N57: Q13.B, LED13.cathode
  N58: R14.Pin_1, Q14.E
  N59: Q14.B, LED14.cathode
  N60: R15.Pin_1, Q15.E
  N61: Q15.B, LED15.cathode
  N62: R16.Pin_1, Q16.E
  N63: Q16.B, LED16.cathode
  N64: R17.Pin_1, Q17.E
  N65: LED17.cathode, Q17.B

notes:
  TIRA DE LED PELDAÑO 1
  TIRA DE LED PELDAÑO 2
  TIRA DE LED PELDAÑO 3
  TIRA DE LED PELDAÑO 4
  TIRA DE LED PELDAÑO 5
  TIRA DE LED PELDAÑO 6
  TIRA DE LED PELDAÑO 7
  TIRA DE LED PELDAÑO 8
  TIRA DE LED PELDAÑO 9
  TIRA DE LED PELDAÑO 10
  TIRA DE LED PELDAÑO 11
  TIRA DE LED PELDAÑO 12
  TIRA DE LED PELDAÑO 13
  TIRA DE LED PELDAÑO 14
  TIRA DE LED PELDAÑO 15
  TIRA DE LED PELDAÑO 16
  TIRA DE LED PELDAÑO 17
  B C E
  BD137
  VCC Trig Echo GND
  HC-SR04
  Sensor
  LDR
  Ajuste
  nivel
  Luz
  10k
  Ajuste
  Velocidad
  10k
  Ajuste
  Distancia
  10k
  12V
  LM7805
  Reloj
  Programador
  Al contacto
  NA
