# Fritzing sketch luz_escalera_ultrasonidos_uno (saved by Fritzing 0.7.7b)

parts:
  Arduino1 = Arduino
  R2 = Resistor [tolerance=±5% resistance=1k package=THT]
  Q2 = NPN-Transistor [package="TO92 [THT]"]
  LED2 = LED - 5mm [color="Red (633nm)" package="5 mm [THT]"]
  R3 = Resistor [tolerance=±5% resistance=1k package=THT]
  Q3 = NPN-Transistor [package="TO92 [THT]"]
  LED3 = LED - 5mm [color="Red (633nm)" package="5 mm [THT]"]
  R4 = Resistor [tolerance=±5% resistance=1k package=THT]
  Q4 = NPN-Transistor [package="TO92 [THT]"]
  LED4 = LED - 5mm [color="Red (633nm)" package="5 mm [THT]"]
  R5 = Resistor [tolerance=±5% resistance=1k package=THT]
  Q5 = NPN-Transistor [package="TO92 [THT]"]
  LED5 = LED - 5mm [color="Red (633nm)" package="5 mm [THT]"]
  R6 = Resistor [tolerance=±5% resistance=1k package=THT]
  Q6 = NPN-Transistor [package="TO92 [THT]"]
  LED6 = LED - 5mm [color="Red (633nm)" package="5 mm [THT]"]
  R7 = Resistor [tolerance=±5% resistance=1k package=THT]
  Q7 = NPN-Transistor [package="TO92 [THT]"]
  LED7 = LED - 5mm [color="Red (633nm)" package="5 mm [THT]"]
  R8 = Resistor [tolerance=±5% resistance=1k package=THT]
  Q8 = NPN-Transistor [package="TO92 [THT]"]
  LED8 = LED - 5mm [color="Red (633nm)" package="5 mm [THT]"]
  R9 = Resistor [tolerance=±5% resistance=1k package=THT]
  Q9 = NPN-Transistor [package="TO92 [THT]"]
  LED9 = LED - 5mm [color="Red (633nm)" package="5 mm [THT]"]
  R10 = Resistor [tolerance=±5% resistance=1k package=THT]
  Q10 = NPN-Transistor [package="TO92 [THT]"]
  LED10 = LED - 5mm [color="Red (633nm)" package="5 mm [THT]"]
  R11 = Trimmer Potentiometer [maximum_resistance=10kΩ package=THT]
  R12 = Trimmer Potentiometer [maximum_resistance=10kΩ package=THT]
  R13 = Trimmer Potentiometer [maximum_resistance=10kΩ package=THT]
  U1 = mystery part, 4 pins [chip_label=?]
  U2 = mystery part, 4 pins [chip_label=?]
  U3 = mystery part, 3 pins [chip_label=?]
  U4 = Voltage Regulator - 5V [package="TO220 [THT]"]
  Power_plug1 = Power plug

nets:
  GND: Arduino1.GND, U1.pin1, U2.pin1, U4.GND, Power_plug1.GND
  N1: Arduino1.D13, U2.pin3
  N2: Arduino1.D12, U2.pin2
  N3: Arduino1.D11, U1.pin3
  N4: Arduino1.D10, U1.pin2
  N5: Arduino1.D8, R10.Pin_0
  N6: Arduino1.D7, R9.Pin_0
  N7: Arduino1.D6, R8.Pin_0
  N8: Arduino1.D5, R7.Pin_0
  N9: Arduino1.D4, R6.Pin_0
  N10: Arduino1.D3, R5.Pin_0
  N11: Arduino1.D2, R4.Pin_0
  N12: Arduino1.D1TX, R3.Pin_0
  N13: Arduino1.D0RX, R2.Pin_0
  N14: Arduino1.VIN, U1.pin4, U2.pin4, U4.output_voltage
  N15: Arduino1.A0, U3.pin2
  N16: Arduino1.A1, R11.wiper
  N17: Arduino1.A2, R12.wiper
  N18: Arduino1.A3, R13.wiper
  N19: R2.Pin_1, Q2.E
  N20: Q2.B, LED2.cathode
  N21: Q2.C, Q3.C, Q4.C, Q5.C, Q6.C, Q7.C, Q8.C, Q9.C, Q10.C, R11.leg1, R12.leg1, R13.leg1, U3.pin1
  N22: LED2.anode, LED3.anode, LED4.anode, LED5.anode, LED6.anode, LED7.anode, LED8.anode, LED9.anode, LED10.anode
  N23: R3.Pin_1, Q3.E
  N24: Q3.B, LED3.cathode
  N25: R4.Pin_1, Q4.E
  N26: Q4.B, LED4.cathode
  N27: R5.Pin_1, Q5.E
  N28: Q5.B, LED5.cathode
  N29: R6.Pin_1, Q6.E
  N30: Q6.B, LED6.cathode
  N31: R7.Pin_1, Q7.E
  N32: Q7.B, LED7.cathode
  N33: R8.Pin_1, Q8.E
  N34: Q8.B, LED8.cathode
  N35: R9.Pin_1, Q9.E
  N36: Q9.B, LED9.cathode
  N37: R10.Pin_1, Q10.E
  N38: Q10.B, LED10.cathode
  N39: R11.leg2, R12.leg2, R13.leg2, U3.pin3

notes:
  TIRA DE LED PELDAÑO 1
  TIRA DE LED PELDAÑO 2
  TIRA DE LED PELDAÑO 3
  TIRA DE LED PELDAÑO 4
  TIRA DE LED PELDAÑO 5
  TIRA DE LED PELDAÑO 6
  TIRA DE LED PELDAÑO 7
  TIRA DE LED PELDAÑO 8
  TIRA DE LED PELDAÑO 9
  GND Echo Trig VCC
  HC-SR04
  Sensor Bajar
  GND Echo Trig VCC
  HC-SR04
  Sensor Subir
  7805
  12V
  Sensor
  Luz
  LDR
  Ajuste
  Nivel
  de luz
  10k
  Ajuste
  Velocidad
  10k
  Ajuste
  Distancia
  10k
  B C E
  BD137
  1K
